# Fritzing sketch CPE301_Assignment3_Schematic (saved by Fritzing 0.9.3b)
breadboards: 1

parts:
  T1 = LM34 Temperature Sensor [package="TO92 [THT]"]
  V2 = DC Power [voltage=5]
  U1 = atmega328 [package=dip]

nets:
  N1: T1.Vout, U1.A0
  GND: T1.GND, V2.V-, U1.GND
  N2: V2.V+, U1.VCC
